# Fritzing sketch Line (saved by Fritzing 0.9.3b)
breadboards: 1

parts:
  U1 = L9110 H-bridge module [part_number="L9110 H-bridge"]
  M1 = DC Motor
  M2 = DC Motor
  부품1 = Arduino Uno (Rev3)
  TCRT2 = TCRT5000 digital module [part_number=151608]
  TCRT3 = TCRT5000 digital module [part_number=151608]
  BAT2 = BC9VPC [package=bc9vpc]
  hc-sr1 = hc-sr04
  hc-sr2 = hc-sr04
  R1 = PHOTOCELL [package=photocell]
  R2 = Resistor [tolerance=±5% resistance=10k package=THT]

nets:
  N1: U1.B-IA, 부품1.D10_PWM/SS
  N2: U1.B-IB, 부품1.D9_PWM
  GND: U1.GND, 부품1.GND, TCRT2.GND, TCRT3.GND, BAT2.V+, hc-sr1.GND, hc-sr2.GND, R1.P$1
  VCC: U1.VCC, 부품1.VIN, BAT2.V-
  N3: U1.A-IA, 부품1.D6_PWM
  N4: U1.A-IB, 부품1.D5_PWM
  N5: U1.MOTOR_A-A, M1.pin_2
  N6: U1.MOTOR_A-B, M1.pin_1
  N7: U1.MOTOR_B-A, M2.pin_2
  N8: U1.MOTOR_B-B, M2.pin_1
  N9: 부품1.A1, R1.P$2, R2.Pin_1
  N10: 부품1.D8, TCRT2.DO1
  N11: 부품1.D11_PWM/MOSI, hc-sr1.Echo
  N12: 부품1.D12/MISO, hc-sr1.Trig
  N13: 부품1.D3_PWM, hc-sr2.Echo
  N14: 부품1.D4, hc-sr2.Trig
  N15: 부품1.D7, TCRT3.DO1
  VCC_2: 부품1.5V, TCRT2.VCC, TCRT3.VCC, hc-sr1.VCC, hc-sr2.VCC, R2.Pin_0

custom parts:
  TCRT5000 digital module: breakout board for TCRT5000 module, convert analog to digital - Uses TCRT5000 infrared reflectance sensor - Detection distance: 1mm~8mm - Focus distance: 2.5mm - Working voltage: 3.3V~12V - Uses wide voltage LM393 comparator - With multi-turn precision potentiometer to adjust the sensitivity - Current: > 15mA - Output type: Digital switch output (0, 1) - Suitable for watt-hour meter pulse data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
